// Logisim project 7_Seg_Driver.circ as structural Verilog: 10 circuits, main circuit main
module main (
  input  in_1,
  input  in_2,
  input  in_3
);

  wire clock_1_out, clock_2_out, n7_seg_driver_1_a, n7_seg_driver_1_b, n7_seg_driver_1_c, n7_seg_driver_1_d,
       n7_seg_driver_1_e, n7_seg_driver_1_f, n7_seg_driver_1_g, n7_seg_driver_2_a, n7_seg_driver_2_b,
       n7_seg_driver_2_c, n7_seg_driver_2_d, n7_seg_driver_2_e, n7_seg_driver_2_f, n7_seg_driver_2_g,
       testing_1_nrco_9, testing_1_q0_15, testing_1_q1_1, testing_1_q2_2, testing_1_q3_3, testing_1_q4_4,
       testing_1_q5_5, testing_1_q6_6, testing_1_q7_7;

  Clock clock_1 (.out(clock_1_out));
  Clock clock_2 (.out(clock_2_out));
  testing testing_1 (
    .CPR_13(clock_2_out), .CPC_11(clock_1_out), .nCE_12(in_1), .nMRC_10(in_2), .nOE_14(in_3),
    .Q0_15(testing_1_q0_15), .Q1_1(testing_1_q1_1), .Q2_2(testing_1_q2_2), .Q3_3(testing_1_q3_3),
    .Q4_4(testing_1_q4_4), .Q5_5(testing_1_q5_5), .Q6_6(testing_1_q6_6), .Q7_7(testing_1_q7_7),
    .nRCO_9(testing_1_nrco_9));
  _7_seg_Driver u_7_seg_driver_1 (
    .a(n7_seg_driver_1_a), .b(n7_seg_driver_1_b), .c(n7_seg_driver_1_c), .d(n7_seg_driver_1_d),
    .e(n7_seg_driver_1_e), .f(n7_seg_driver_1_f), .g(n7_seg_driver_1_g), .B0(testing_1_q0_15),
    .B1(testing_1_q1_1), .B2(testing_1_q2_2), .B3(testing_1_q3_3));
  _7_seg_Driver u_7_seg_driver_2 (
    .a(n7_seg_driver_2_a), .b(n7_seg_driver_2_b), .c(n7_seg_driver_2_c), .d(n7_seg_driver_2_d),
    .e(n7_seg_driver_2_e), .f(n7_seg_driver_2_f), .g(n7_seg_driver_2_g), .B0(testing_1_q4_4),
    .B1(testing_1_q5_5), .B2(testing_1_q6_6), .B3(testing_1_q7_7));
  _7_Segment_Display u_7_segment_display_1 (
    .g(n7_seg_driver_1_g), .f(n7_seg_driver_1_f), .a(n7_seg_driver_1_a), .b(n7_seg_driver_1_b),
    .e(n7_seg_driver_1_e), .d(n7_seg_driver_1_d), .c(n7_seg_driver_1_c));  // open: dp
  _7_Segment_Display u_7_segment_display_2 (
    .g(n7_seg_driver_2_g), .f(n7_seg_driver_2_f), .a(n7_seg_driver_2_a), .b(n7_seg_driver_2_b),
    .e(n7_seg_driver_2_e), .d(n7_seg_driver_2_d), .c(n7_seg_driver_2_c), .dp(testing_1_nrco_9));
endmodule

// s_A
module seg_A (
  input  b0,
  input  b1,
  input  b2,
  input  b3,
  output a
);

  wire and_1_out, and_2_out, and_3_out, and_4_out, and_5_out, and_6_out, not_1_out, not_2_out, not_3_out,
       not_4_out, not_5_out, not_6_out, not_7_out;

  not not_1 (not_1_out, b1);
  and and_1 (and_1_out, not_1_out, not_2_out);
  not not_2 (not_2_out, b3);
  not not_3 (not_3_out, b0);
  and and_2 (and_2_out, not_3_out, b2);
  not not_4 (not_4_out, b0);
  and and_3 (and_3_out, not_4_out, b1, b3);
  and and_4 (and_4_out, b1, b2);
  not not_5 (not_5_out, b1);
  and and_5 (and_5_out, b0, not_5_out, not_6_out);
  not not_6 (not_6_out, b2);
  and and_6 (and_6_out, b0, not_7_out);
  not not_7 (not_7_out, b3);
  or or_1 (a, and_1_out, and_2_out, and_3_out, and_4_out, and_5_out, and_6_out);
endmodule

// s_B
module seg_B (
  input  b0,
  input  b1,
  input  b2,
  input  b3,
  output b
);

  wire and_1_out, and_2_out, and_3_out, and_4_out, and_5_out, and_6_out, not_1_out, not_2_out, not_3_out,
       not_4_out, not_5_out, not_6_out, not_7_out, not_8_out, not_9_out, not_10_out, not_11_out;

  not not_1 (not_1_out, b0);
  and and_1 (and_1_out, not_1_out, not_2_out);
  not not_2 (not_2_out, b1);
  not not_3 (not_3_out, b0);
  not not_4 (not_4_out, b2);
  and and_2 (and_2_out, not_3_out, not_4_out, not_5_out);
  not not_5 (not_5_out, b3);
  not not_6 (not_6_out, b1);
  and and_3 (and_3_out, not_6_out, not_7_out);
  not not_7 (not_7_out, b2);
  not not_8 (not_8_out, b1);
  and and_4 (and_4_out, not_8_out, not_9_out);
  not not_9 (not_9_out, b3);
  not not_10 (not_10_out, b0);
  and and_5 (and_5_out, not_10_out, b2, b3);
  and and_6 (and_6_out, b0, not_11_out, b3);
  not not_11 (not_11_out, b2);
  or or_1 (b, and_1_out, and_2_out, and_3_out, and_4_out, and_5_out, and_6_out);
endmodule

// s_C
module seg_C (
  input  b0,
  input  b1,
  input  b2,
  input  b3,
  output c
);

  wire and_1_out, and_2_out, and_3_out, and_4_out, and_5_out, not_1_out, not_2_out, not_3_out, not_4_out,
       not_5_out, not_6_out;

  not not_1 (not_1_out, b0);
  and and_1 (and_1_out, not_1_out, not_2_out);
  not not_2 (not_2_out, b2);
  not not_3 (not_3_out, b0);
  and and_2 (and_2_out, not_3_out, b3);
  not not_4 (not_4_out, b2);
  and and_3 (and_3_out, not_4_out, b3);
  not not_5 (not_5_out, b0);
  and and_4 (and_4_out, not_5_out, b1);
  and and_5 (and_5_out, b0, not_6_out);
  not not_6 (not_6_out, b1);
  or or_1 (c, and_1_out, and_2_out, and_3_out, and_4_out, and_5_out);
endmodule

// s_D
module seg_D (
  input  b0,
  input  b1,
  input  b2,
  input  b3,
  output d
);

  wire and_1_out, and_2_out, and_3_out, and_4_out, and_5_out, not_1_out, not_2_out, not_3_out, not_4_out,
       not_5_out, not_6_out, not_7_out;

  not not_1 (not_1_out, b0);
  not not_2 (not_2_out, b1);
  and and_1 (and_1_out, not_1_out, not_2_out, not_3_out);
  not not_3 (not_3_out, b3);
  not not_4 (not_4_out, b1);
  and and_2 (and_2_out, not_4_out, b2, b3);
  and and_3 (and_3_out, b1, not_5_out, b3);
  not not_5 (not_5_out, b2);
  and and_4 (and_4_out, b1, b2, not_6_out);
  not not_6 (not_6_out, b3);
  and and_5 (and_5_out, b0, not_7_out);
  not not_7 (not_7_out, b2);
  or or_1 (d, and_1_out, and_2_out, and_3_out, and_4_out, and_5_out);
endmodule

// s_E
module seg_E (
  input  b0,
  input  b1,
  input  b2,
  input  b3,
  output e
);

  wire and_1_out, and_2_out, and_3_out, and_4_out, not_1_out, not_2_out, not_3_out;

  not not_1 (not_1_out, b1);
  and and_1 (and_1_out, not_1_out, not_2_out);
  not not_2 (not_2_out, b3);
  and and_2 (and_2_out, b2, not_3_out);
  not not_3 (not_3_out, b3);
  and and_3 (and_3_out, b0, b2);
  and and_4 (and_4_out, b0, b1);
  or or_1 (e, and_1_out, and_2_out, and_3_out, and_4_out);
endmodule

// s_F
module seg_F (
  input  b0,
  input  b1,
  input  b2,
  input  b3,
  output f
);

  wire and_1_out, and_2_out, and_3_out, and_4_out, and_5_out, not_1_out, not_2_out, not_3_out, not_4_out,
       not_5_out, not_6_out;

  not not_1 (not_1_out, b2);
  and and_1 (and_1_out, not_1_out, not_2_out);
  not not_2 (not_2_out, b3);
  not not_3 (not_3_out, b0);
  and and_2 (and_2_out, not_3_out, b1, not_4_out);
  not not_4 (not_4_out, b2);
  and and_3 (and_3_out, b1, not_5_out);
  not not_5 (not_5_out, b3);
  and and_4 (and_4_out, b0, not_6_out);
  not not_6 (not_6_out, b1);
  and and_5 (and_5_out, b0, b2);
  or or_1 (f, and_1_out, and_2_out, and_3_out, and_4_out, and_5_out);
endmodule

// s_G
module seg_G (
  input  b0,
  input  b1,
  input  b2,
  input  b3,
  output g
);

  wire and_1_out, and_2_out, and_3_out, and_4_out, and_5_out, not_1_out, not_2_out, not_3_out, not_4_out,
       not_5_out;

  not not_1 (not_1_out, b1);
  and and_1 (and_1_out, not_1_out, b2);
  and and_2 (and_2_out, b2, not_2_out);
  not not_2 (not_2_out, b3);
  not not_3 (not_3_out, b0);
  and and_3 (and_3_out, not_3_out, b1, not_4_out);
  not not_4 (not_4_out, b2);
  and and_4 (and_4_out, b0, not_5_out);
  not not_5 (not_5_out, b1);
  and and_5 (and_5_out, b0, b3);
  or or_1 (g, and_1_out, and_2_out, and_3_out, and_4_out, and_5_out);
endmodule

// 7_Seg_Driver
module _7_seg_Driver (
  input  B0,
  input  B1,
  input  B2,
  input  B3,
  output a,
  output b,
  output c,
  output d,
  output e,
  output f,
  output g
);

  seg_A seg_a_1 (.b0(B3), .b1(B2), .b2(B1), .b3(B0), .a(a));
  seg_B seg_b_1 (.b0(B3), .b1(B2), .b2(B1), .b3(B0), .b(b));
  seg_C seg_c_1 (.b0(B3), .b1(B2), .b2(B1), .b3(B0), .c(c));
  seg_D seg_d_1 (.b0(B3), .b1(B2), .b2(B1), .b3(B0), .d(d));
  seg_E seg_e_1 (.b0(B3), .b1(B2), .b2(B1), .b3(B0), .e(e));
  seg_F seg_f_1 (.b0(B3), .b1(B2), .b2(B1), .b3(B0), .f(f));
  seg_G seg_g_1 (.b0(B3), .b1(B2), .b2(B1), .b3(B0), .g(g));
endmodule

module testing (
  input  CPR_13,
  input  CPC_11,
  input  nCE_12,
  input  nMRC_10,
  input  nOE_14,
  output Q0_15,
  output Q1_1,
  output Q2_2,
  output Q3_3,
  output Q4_4,
  output Q5_5,
  output Q6_6,
  output Q7_7,
  output nRCO_9
);

  wire and_1_out, and_2_out, j_k_ff_1_qn, j_k_ff_2_qn, j_k_ff_3_qn, j_k_ff_4_qn, j_k_ff_5_qn, j_k_ff_6_qn,
       j_k_ff_7_qn, not_1_out, not_2_out, not_3_out, undriven;
  wire [7:0] j_k_ff_1_q, register_1_q;

  J_K_Flip_Flop j_k_ff_1 (
    .J(not_1_out), .clk(CPC_11), .K(not_1_out), .Q(j_k_ff_1_q[0]), .Qn(j_k_ff_1_qn), .preset(1'b0),
    .reset(undriven));  // open: en
  not not_1 (not_1_out, nCE_12);
  not not_2 (not_2_out, nMRC_10);
  not not_3 (not_3_out, nOE_14);
  J_K_Flip_Flop j_k_ff_2 (
    .J(not_1_out), .clk(j_k_ff_1_qn), .K(not_1_out), .Q(j_k_ff_1_q[1]), .Qn(j_k_ff_2_qn), .preset(1'b0),
    .reset(undriven));  // open: en
  J_K_Flip_Flop j_k_ff_3 (
    .J(not_1_out), .clk(j_k_ff_2_qn), .K(not_1_out), .Q(j_k_ff_1_q[2]), .Qn(j_k_ff_3_qn), .preset(1'b0),
    .reset(undriven));  // open: en
  J_K_Flip_Flop j_k_ff_4 (
    .J(not_1_out), .clk(j_k_ff_3_qn), .K(not_1_out), .Q(j_k_ff_1_q[3]), .Qn(j_k_ff_4_qn), .preset(1'b0),
    .reset(undriven));  // open: en
  J_K_Flip_Flop j_k_ff_5 (
    .J(not_1_out), .clk(j_k_ff_4_qn), .K(not_1_out), .Q(j_k_ff_1_q[4]), .Qn(j_k_ff_5_qn), .preset(1'b0),
    .reset(undriven));  // open: en
  J_K_Flip_Flop j_k_ff_6 (
    .J(not_1_out), .clk(j_k_ff_5_qn), .K(not_1_out), .Q(j_k_ff_1_q[5]), .Qn(j_k_ff_6_qn), .preset(1'b0),
    .reset(undriven));  // open: en
  J_K_Flip_Flop j_k_ff_7 (
    .J(not_1_out), .clk(j_k_ff_6_qn), .K(not_1_out), .Q(j_k_ff_1_q[6]), .Qn(j_k_ff_7_qn), .preset(1'b0),
    .reset(undriven));  // open: en
  and and_1 (and_1_out, j_k_ff_1_q[0], j_k_ff_1_q[1], j_k_ff_1_q[2], j_k_ff_1_q[3], j_k_ff_1_q[4], j_k_ff_1_q[5], j_k_ff_1_q[6], j_k_ff_1_q[7], j_k_ff_1_q[7]);
  J_K_Flip_Flop j_k_ff_8 (
    .J(not_1_out), .clk(j_k_ff_7_qn), .K(not_1_out), .Q(j_k_ff_1_q[7]), .preset(1'b0), .reset(undriven));  // open: Qn, en
  and and_2 (and_2_out, j_k_ff_1_q[3], j_k_ff_1_q[1]);
  assign {Q7_7, Q6_6, Q5_5, Q4_4, Q3_3, Q2_2, Q1_1, Q0_15} = not_3_out ? register_1_q : 8'bz;  // Controlled_Buffer controlled_buffer_1
  Register register_1 (.D(j_k_ff_1_q), .Q(register_1_q), .clk(CPR_13), .clr(undriven));  // open: en
  not not_4 (nRCO_9, and_1_out);

  // Notes on the sheet:
  //   nOE_14: pull=up
endmodule
