// Logisim project Counter driver.circ as structural Verilog: 2 circuits, main circuit main
module main (
  input  in_1,
  input  in_2
);

  wire counter_driver_1_q1, counter_driver_1_q2, counter_driver_1_q3, counter_driver_1_q4,
       counter_driver_1_q5, counter_driver_1_q6, counter_driver_1_q7, counter_driver_1_q8, n7_seg_driver_1_a,
       n7_seg_driver_1_b, n7_seg_driver_1_c, n7_seg_driver_1_d, n7_seg_driver_1_e, n7_seg_driver_1_f,
       n7_seg_driver_1_g, n7_seg_driver_2_a, n7_seg_driver_2_b, n7_seg_driver_2_c, n7_seg_driver_2_d,
       n7_seg_driver_2_e, n7_seg_driver_2_f, n7_seg_driver_2_g;

  Counter_driver counter_driver_1 (
    .\UP_DƠN (in_1), .SIGNAL(in_2), .Q1(counter_driver_1_q1), .Q2(counter_driver_1_q2),
    .Q7(counter_driver_1_q7), .Q8(counter_driver_1_q8), .Q4(counter_driver_1_q4), .Q5(counter_driver_1_q5),
    .Q3(counter_driver_1_q3), .Q6(counter_driver_1_q6));
  _7_seg_Driver u_7_seg_driver_1 (
    .a(n7_seg_driver_1_a), .b(n7_seg_driver_1_b), .c(n7_seg_driver_1_c), .d(n7_seg_driver_1_d),
    .e(n7_seg_driver_1_e), .f(n7_seg_driver_1_f), .g(n7_seg_driver_1_g), .B0(counter_driver_1_q1),
    .B1(counter_driver_1_q2), .B2(counter_driver_1_q3), .B3(counter_driver_1_q4));
  _7_seg_Driver u_7_seg_driver_2 (
    .a(n7_seg_driver_2_a), .b(n7_seg_driver_2_b), .c(n7_seg_driver_2_c), .d(n7_seg_driver_2_d),
    .e(n7_seg_driver_2_e), .f(n7_seg_driver_2_f), .g(n7_seg_driver_2_g), .B0(counter_driver_1_q5),
    .B1(counter_driver_1_q6), .B2(counter_driver_1_q7), .B3(counter_driver_1_q8));
  _7_Segment_Display u_7_segment_display_1 (
    .g(n7_seg_driver_1_g), .f(n7_seg_driver_1_f), .a(n7_seg_driver_1_a), .b(n7_seg_driver_1_b),
    .e(n7_seg_driver_1_e), .d(n7_seg_driver_1_d), .c(n7_seg_driver_1_c));  // open: dp
  _7_Segment_Display u_7_segment_display_2 (
    .g(n7_seg_driver_2_g), .f(n7_seg_driver_2_f), .a(n7_seg_driver_2_a), .b(n7_seg_driver_2_b),
    .e(n7_seg_driver_2_e), .d(n7_seg_driver_2_d), .c(n7_seg_driver_2_c));  // open: dp
endmodule

module Counter_driver (
  input  \UP_DƠN ,
  input  SIGNAL,
  output Q1,
  output Q2,
  output Q7,
  output Q8,
  output Q4,
  output Q5,
  output Q3,
  output Q6
);

  wire and_1_out, and_2_out, and_3_out, and_4_out, and_5_out, and_6_out, and_7_out, and_8_out, and_9_out,
       and_10_out, and_11_out, and_12_out, and_13_out, and_14_out, and_15_out, and_16_out, and_17_out,
       j_k_ff_1_qn, j_k_ff_2_qn, j_k_ff_3_qn, j_k_ff_5_qn, j_k_ff_6_qn, j_k_ff_7_qn, nand_1_out, nand_2_out,
       not_1_out, not_2_out, or_1_out, or_2_out, or_3_out, or_4_out, or_5_out, or_6_out;

  and and_1 (and_1_out, and_2_out, and_9_out);
  not not_1 (not_1_out, \UP_DƠN );
  and and_2 (and_2_out, Q4, Q3, Q2, Q1);
  J_K_Flip_Flop j_k_ff_1 (
    .J(1'b1), .clk(SIGNAL), .K(1'b1), .Q(Q1), .Qn(j_k_ff_1_qn), .preset(and_1_out), .en(nand_2_out),
    .reset(and_9_out));
  and and_3 (and_3_out, not_1_out, Q1);
  and and_4 (and_4_out, j_k_ff_1_qn, \UP_DƠN );
  or or_1 (or_1_out, and_3_out, and_4_out);
  J_K_Flip_Flop j_k_ff_2 (
    .J(or_1_out), .clk(SIGNAL), .K(or_1_out), .Q(Q2), .Qn(j_k_ff_2_qn), .en(nand_2_out), .reset(and_9_out));  // open: preset
  and and_5 (and_5_out, and_3_out, Q2);
  and and_6 (and_6_out, j_k_ff_2_qn, and_4_out);
  or or_2 (or_2_out, and_5_out, and_6_out);
  J_K_Flip_Flop j_k_ff_3 (
    .J(or_2_out), .clk(SIGNAL), .K(or_2_out), .Q(Q3), .Qn(j_k_ff_3_qn), .en(nand_2_out), .reset(and_9_out));  // open: preset
  and and_7 (and_7_out, and_5_out, Q3);
  and and_8 (and_8_out, j_k_ff_3_qn, and_6_out);
  and and_9 (and_9_out, Q2, Q4);
  or or_3 (or_3_out, and_7_out, and_8_out);
  J_K_Flip_Flop j_k_ff_4 (
    .J(or_3_out), .clk(SIGNAL), .K(or_3_out), .Q(Q4), .preset(and_1_out), .en(nand_2_out), .reset(and_9_out));  // open: Qn
  and and_10 (and_10_out, Q4, Q2);
  nand nand_1 (nand_1_out, Q4, Q3, Q2, Q1);
  not not_2 (not_2_out, \UP_DƠN );
  J_K_Flip_Flop j_k_ff_5 (
    .J(1'b1), .clk(and_10_out), .K(1'b1), .Q(Q5), .Qn(j_k_ff_5_qn), .en(nand_2_out));  // open: preset, reset
  and and_11 (and_11_out, not_2_out, Q5);
  and and_12 (and_12_out, j_k_ff_5_qn, \UP_DƠN );
  nand nand_2 (nand_2_out, nand_1_out, and_13_out);
  or or_4 (or_4_out, and_11_out, and_12_out);
  and and_13 (and_13_out, Q5, Q7);
  J_K_Flip_Flop j_k_ff_6 (
    .J(or_4_out), .clk(and_10_out), .K(or_4_out), .Q(Q6), .Qn(j_k_ff_6_qn), .en(nand_2_out));  // open: preset, reset
  and and_14 (and_14_out, and_11_out, Q6);
  and and_15 (and_15_out, j_k_ff_6_qn, and_12_out);
  or or_5 (or_5_out, and_14_out, and_15_out);
  J_K_Flip_Flop j_k_ff_7 (
    .J(or_5_out), .clk(and_10_out), .K(or_5_out), .Q(Q7), .Qn(j_k_ff_7_qn), .en(nand_2_out));  // open: preset, reset
  and and_16 (and_16_out, j_k_ff_7_qn, and_15_out);
  and and_17 (and_17_out, and_14_out, Q7);
  or or_6 (or_6_out, and_17_out, and_16_out);
  J_K_Flip_Flop j_k_ff_8 (
    .J(or_6_out), .clk(and_10_out), .K(or_6_out), .Q(Q8), .en(nand_2_out));  // open: Qn, preset, reset
endmodule
