// Logisim project Counter.circ as structural Verilog: 1 circuit, main circuit main
module main (
  input  in_1
);

  wire and_1_out, and_2_out, and_3_out, and_4_out, and_5_out, and_6_out, and_7_out, and_8_out, and_9_out,
       and_10_out, and_11_out, and_12_out, and_13_out, and_14_out, and_15_out, and_16_out, and_17_out,
       clock_1_out, j_k_ff_1_q, j_k_ff_1_qn, j_k_ff_2_q, j_k_ff_2_qn, j_k_ff_3_q, j_k_ff_3_qn, j_k_ff_4_q,
       j_k_ff_5_q, j_k_ff_5_qn, j_k_ff_6_q, j_k_ff_6_qn, j_k_ff_7_q, j_k_ff_7_qn, j_k_ff_8_q,
       n7_seg_driver_1_a, n7_seg_driver_1_b, n7_seg_driver_1_c, n7_seg_driver_1_d, n7_seg_driver_1_e,
       n7_seg_driver_1_f, n7_seg_driver_1_g, n7_seg_driver_2_a, n7_seg_driver_2_b, n7_seg_driver_2_c,
       n7_seg_driver_2_d, n7_seg_driver_2_e, n7_seg_driver_2_f, n7_seg_driver_2_g, not_1_out, not_2_out,
       or_1_out, or_2_out, or_3_out, or_4_out, or_5_out, or_6_out, undriven, undriven_2;

  Clock clock_1 (.out(clock_1_out));
  and and_1 (and_1_out, and_9_out, and_2_out);
  not not_1 (not_1_out, in_1);
  J_K_Flip_Flop j_k_ff_1 (
    .J(1'b1), .clk(clock_1_out), .K(1'b1), .Q(j_k_ff_1_q), .Qn(j_k_ff_1_qn), .preset(and_1_out),
    .reset(and_9_out));  // open: en
  and and_2 (and_2_out, j_k_ff_3_q, j_k_ff_1_q, j_k_ff_4_q, j_k_ff_2_q);
  and and_3 (and_3_out, not_1_out, j_k_ff_1_q);
  and and_4 (and_4_out, in_1, j_k_ff_1_qn);
  or or_1 (or_1_out, and_3_out, and_4_out);
  J_K_Flip_Flop j_k_ff_2 (
    .J(or_1_out), .clk(clock_1_out), .K(or_1_out), .Q(j_k_ff_2_q), .Qn(j_k_ff_2_qn), .reset(and_9_out));  // open: preset, en
  and and_5 (and_5_out, and_3_out, j_k_ff_2_q);
  and and_6 (and_6_out, j_k_ff_2_qn, and_4_out);
  or or_2 (or_2_out, and_5_out, and_6_out);
  _7_seg_Driver u_7_seg_driver_1 (
    .a(n7_seg_driver_1_a), .b(n7_seg_driver_1_b), .c(n7_seg_driver_1_c), .d(n7_seg_driver_1_d),
    .e(n7_seg_driver_1_e), .f(n7_seg_driver_1_f), .g(n7_seg_driver_1_g), .B0(j_k_ff_1_q), .B1(j_k_ff_2_q),
    .B2(j_k_ff_3_q), .B3(j_k_ff_4_q));
  J_K_Flip_Flop j_k_ff_3 (
    .J(or_2_out), .clk(clock_1_out), .K(or_2_out), .Q(j_k_ff_3_q), .Qn(j_k_ff_3_qn), .reset(and_9_out));  // open: preset, en
  _7_Segment_Display u_7_segment_display_1 (
    .g(n7_seg_driver_1_g), .f(n7_seg_driver_1_f), .a(n7_seg_driver_1_a), .b(n7_seg_driver_1_b),
    .e(n7_seg_driver_1_e), .d(n7_seg_driver_1_d), .c(n7_seg_driver_1_c));  // open: dp
  and and_7 (and_7_out, and_5_out, j_k_ff_3_q);
  and and_8 (and_8_out, j_k_ff_3_qn, and_6_out);
  J_K_Flip_Flop j_k_ff_4 (
    .J(or_3_out), .clk(clock_1_out), .K(or_3_out), .Q(j_k_ff_4_q), .preset(and_1_out), .reset(and_9_out));  // open: Qn, en
  or or_3 (or_3_out, and_7_out, and_8_out);
  and and_9 (and_9_out, j_k_ff_4_q, j_k_ff_2_q);
  and and_10 (and_10_out, j_k_ff_4_q, j_k_ff_2_q);
  not not_2 (not_2_out, in_1);
  J_K_Flip_Flop j_k_ff_5 (
    .J(1'b1), .clk(and_10_out), .K(1'b1), .Q(j_k_ff_5_q), .Qn(j_k_ff_5_qn), .reset(undriven));  // open: preset, en
  and and_11 (and_11_out, not_2_out, j_k_ff_5_q);
  and and_12 (and_12_out, in_1, j_k_ff_5_qn);
  or or_4 (or_4_out, and_11_out, and_12_out);
  J_K_Flip_Flop j_k_ff_6 (
    .J(or_4_out), .clk(and_10_out), .K(or_4_out), .Q(j_k_ff_6_q), .Qn(j_k_ff_6_qn), .reset(undriven));  // open: preset, en
  and and_13 (and_13_out, and_11_out, j_k_ff_6_q);
  and and_14 (and_14_out, j_k_ff_6_qn, and_12_out);
  or or_5 (or_5_out, and_13_out, and_14_out);
  _7_seg_Driver u_7_seg_driver_2 (
    .a(n7_seg_driver_2_a), .b(n7_seg_driver_2_b), .c(n7_seg_driver_2_c), .d(n7_seg_driver_2_d),
    .e(n7_seg_driver_2_e), .f(n7_seg_driver_2_f), .g(n7_seg_driver_2_g), .B0(j_k_ff_5_q), .B1(j_k_ff_6_q),
    .B2(j_k_ff_7_q), .B3(j_k_ff_8_q));
  J_K_Flip_Flop j_k_ff_7 (
    .J(or_5_out), .clk(and_10_out), .K(or_5_out), .Q(j_k_ff_7_q), .Qn(j_k_ff_7_qn), .reset(undriven));  // open: preset, en
  _7_Segment_Display u_7_segment_display_2 (
    .g(n7_seg_driver_2_g), .f(n7_seg_driver_2_f), .a(n7_seg_driver_2_a), .b(n7_seg_driver_2_b),
    .e(n7_seg_driver_2_e), .d(n7_seg_driver_2_d), .c(n7_seg_driver_2_c));  // open: dp
  and and_15 (and_15_out, and_13_out, j_k_ff_7_q);
  and and_16 (and_16_out, j_k_ff_7_qn, and_14_out);
  J_K_Flip_Flop j_k_ff_8 (
    .J(or_6_out), .clk(and_10_out), .K(or_6_out), .Q(j_k_ff_8_q), .reset(undriven_2));  // open: Qn, preset, en
  or or_6 (or_6_out, and_15_out, and_16_out);
  and and_17 (and_17_out, j_k_ff_7_q, j_k_ff_6_q);
endmodule
