// Logisim project Fee drive.circ as structural Verilog: 3 circuits, main circuit main
module main (
  input  in_1,
  input  in_2
);

  wire fee_result_1_out_3, fee_result_1_out_4, fee_result_1_out_5, fee_result_1_out_6, fee_result_1_out_7,
       fee_result_1_out_8, fee_result_1_out_9, fee_result_1_out_10, fee_result_1_out_11, fee_result_1_out_12,
       fee_result_1_out_13, fee_result_1_out_14, n7_seg_driver_1_a, n7_seg_driver_1_b, n7_seg_driver_1_c,
       n7_seg_driver_1_d, n7_seg_driver_1_e, n7_seg_driver_1_f, n7_seg_driver_1_g, n7_seg_driver_2_a,
       n7_seg_driver_2_b, n7_seg_driver_2_c, n7_seg_driver_2_d, n7_seg_driver_2_e, n7_seg_driver_2_f,
       n7_seg_driver_2_g, n7_seg_driver_3_a, n7_seg_driver_3_b, n7_seg_driver_3_c, n7_seg_driver_3_d,
       n7_seg_driver_3_e, n7_seg_driver_3_f, n7_seg_driver_3_g;

  Fee_result fee_result_1 (
    .in_1(in_1), .in_2(in_2), .out_3(fee_result_1_out_3), .out_4(fee_result_1_out_4),
    .out_5(fee_result_1_out_5), .out_6(fee_result_1_out_6), .out_7(fee_result_1_out_7),
    .out_8(fee_result_1_out_8), .out_9(fee_result_1_out_9), .out_10(fee_result_1_out_10),
    .out_11(fee_result_1_out_11), .out_12(fee_result_1_out_12), .out_13(fee_result_1_out_13),
    .out_14(fee_result_1_out_14));
  _7_seg_Driver u_7_seg_driver_1 (
    .a(n7_seg_driver_1_a), .b(n7_seg_driver_1_b), .c(n7_seg_driver_1_c), .d(n7_seg_driver_1_d),
    .e(n7_seg_driver_1_e), .f(n7_seg_driver_1_f), .g(n7_seg_driver_1_g), .B0(fee_result_1_out_3),
    .B1(fee_result_1_out_4), .B2(fee_result_1_out_5), .B3(fee_result_1_out_6));
  _7_seg_Driver u_7_seg_driver_2 (
    .a(n7_seg_driver_2_a), .b(n7_seg_driver_2_b), .c(n7_seg_driver_2_c), .d(n7_seg_driver_2_d),
    .e(n7_seg_driver_2_e), .f(n7_seg_driver_2_f), .g(n7_seg_driver_2_g), .B0(fee_result_1_out_7),
    .B1(fee_result_1_out_8), .B2(fee_result_1_out_9), .B3(fee_result_1_out_10));
  _7_seg_Driver u_7_seg_driver_3 (
    .a(n7_seg_driver_3_a), .b(n7_seg_driver_3_b), .c(n7_seg_driver_3_c), .d(n7_seg_driver_3_d),
    .e(n7_seg_driver_3_e), .f(n7_seg_driver_3_f), .g(n7_seg_driver_3_g), .B0(fee_result_1_out_11),
    .B1(fee_result_1_out_12), .B2(fee_result_1_out_13), .B3(fee_result_1_out_14));
  _7_Segment_Display u_7_segment_display_1 (
    .g(n7_seg_driver_1_g), .f(n7_seg_driver_1_f), .a(n7_seg_driver_1_a), .b(n7_seg_driver_1_b),
    .e(n7_seg_driver_1_e), .d(n7_seg_driver_1_d), .c(n7_seg_driver_1_c));  // open: dp
  _7_Segment_Display u_7_segment_display_2 (
    .g(n7_seg_driver_2_g), .f(n7_seg_driver_2_f), .a(n7_seg_driver_2_a), .b(n7_seg_driver_2_b),
    .e(n7_seg_driver_2_e), .d(n7_seg_driver_2_d), .c(n7_seg_driver_2_c));  // open: dp
  _7_Segment_Display u_7_segment_display_3 (
    .g(n7_seg_driver_3_g), .f(n7_seg_driver_3_f), .a(n7_seg_driver_3_a), .b(n7_seg_driver_3_b),
    .e(n7_seg_driver_3_e), .d(n7_seg_driver_3_d), .c(n7_seg_driver_3_c));  // open: dp
endmodule

module Fee_circut (
  input  SIGNAL,
  input  Reset,
  output Q1,
  output Q2,
  output Q4,
  output Q3
);

  wire and_1_out, and_2_out, and_3_out, and_4_out, and_5_out, and_6_out, j_k_ff_1_qn, j_k_ff_2_qn,
       j_k_ff_3_qn, not_1_out, or_1_out, or_2_out, or_3_out;

  not not_1 (not_1_out, 1'b0);
  J_K_Flip_Flop j_k_ff_1 (
    .J(1'b1), .clk(SIGNAL), .K(1'b1), .Q(Q1), .Qn(j_k_ff_1_qn), .reset(Reset));  // open: preset, en
  and and_1 (and_1_out, not_1_out, Q1);
  and and_2 (and_2_out, j_k_ff_1_qn, 1'b0);
  or or_1 (or_1_out, and_1_out, and_2_out);
  J_K_Flip_Flop j_k_ff_2 (
    .J(or_1_out), .clk(SIGNAL), .K(or_1_out), .Q(Q2), .Qn(j_k_ff_2_qn), .reset(Reset));  // open: preset, en
  and and_3 (and_3_out, and_1_out, Q2);
  and and_4 (and_4_out, j_k_ff_2_qn, and_2_out);
  or or_2 (or_2_out, and_3_out, and_4_out);
  J_K_Flip_Flop j_k_ff_3 (
    .J(or_2_out), .clk(SIGNAL), .K(or_2_out), .Q(Q3), .Qn(j_k_ff_3_qn), .reset(Reset));  // open: preset, en
  and and_5 (and_5_out, and_3_out, Q3);
  and and_6 (and_6_out, j_k_ff_3_qn, and_4_out);
  or or_3 (or_3_out, and_5_out, and_6_out);
  J_K_Flip_Flop j_k_ff_4 (.J(or_3_out), .clk(SIGNAL), .K(or_3_out), .Q(Q4), .reset(Reset));  // open: Qn, preset, en
endmodule

module Fee_result (
  input  in_1,
  input  in_2,
  output out_3,
  output out_4,
  output out_5,
  output out_6,
  output out_7,
  output out_8,
  output out_9,
  output out_10,
  output out_11,
  output out_12,
  output out_13,
  output out_14
);

  wire and_1_out, and_2_out, and_3_out, and_4_out, or_1_out, or_2_out, or_3_out;

  or or_1 (or_1_out, in_2, and_2_out);
  or or_2 (or_2_out, in_2, and_3_out);
  or or_3 (or_3_out, in_2, and_4_out);
  and and_1 (and_1_out, and_2_out, and_3_out, and_2_out);
  Fee_circut fee_circut_1 (.SIGNAL(in_1), .Reset(or_1_out), .Q1(out_3), .Q2(out_4), .Q4(out_6), .Q3(out_5));
  Fee_circut fee_circut_2 (.SIGNAL(and_2_out), .Reset(or_2_out), .Q1(out_7), .Q2(out_8), .Q4(out_10), .Q3(out_9));
  Fee_circut fee_circut_3 (.SIGNAL(and_1_out), .Reset(or_3_out), .Q1(out_11), .Q2(out_12), .Q4(out_14), .Q3(out_13));
  and and_2 (and_2_out, out_4, out_6);
  and and_3 (and_3_out, out_8, out_10);
  and and_4 (and_4_out, out_12, out_14);
endmodule
