// Logisim project Main.circ as structural Verilog: 2 circuits, main circuit main
module main (
  input  in_1,
  input  in_2,
  input  in_3,
  input  in_4,
  input  in_5,
  input  in_6,
  input  in_7,
  input  in_8,
  input  in_9,
  input  in_10,
  input  in_11,
  input  in_12,
  input  in_13,
  input  in_14,
  input  in_15,
  input  in_16,
  input  in_17
);

  wire and_1_out, and_2_out, and_3_out, and_4_out, and_5_out, b2d_1_a_2, b2d_1_b_2, b2d_1_c_2, b2d_1_d_2,
       b2d_1_e, b2d_1_f, b2d_1_g, b2d_2_a_2, b2d_2_b_2, b2d_2_c_2, b2d_2_d_2, b2d_2_e, b2d_2_f, b2d_2_g,
       b2d_3_a_2, b2d_3_b_2, b2d_3_c_2, b2d_3_d_2, b2d_3_e, b2d_3_f, b2d_3_g, b2d_4_a_2, b2d_4_b_2,
       b2d_4_c_2, b2d_4_d_2, b2d_4_e, b2d_4_f, b2d_4_g, clock_1_out, clock_control_1_p1, clock_control_1_p2,
       clock_control_1_p3, clock_control_1_p4, clock_control_1_p5, clock_control_1_p6, clock_control_1_p7,
       clock_control_1_p8, clock_control_1_p9, clock_control_1_p10, clock_control_1_p11, clock_control_1_p12,
       clock_control_1_p13, clock_control_1_p14, clock_control_1_p15, clock_control_1_p16,
       clock_control_1_p17, clock_control_1_p18, clock_control_1_p19, clock_control_1_p20,
       clock_control_1_p21, clock_control_1_p22, clock_control_1_p23, clock_control_1_p24,
       clock_control_1_p25, clock_control_1_p26, clock_control_1_p27, clock_control_1_p28,
       clock_control_1_p29, clock_control_1_p30, counter_driver_1_q1, counter_driver_1_q2,
       counter_driver_1_q3, counter_driver_1_q4, counter_driver_1_q5, counter_driver_1_q6,
       counter_driver_1_q7, counter_driver_1_q8, j_k_ff_1_q, n7_seg_driver_1_a, n7_seg_driver_1_b,
       n7_seg_driver_1_c, n7_seg_driver_1_d, n7_seg_driver_1_e, n7_seg_driver_1_f, n7_seg_driver_1_g,
       n7_seg_driver_2_a, n7_seg_driver_2_b, n7_seg_driver_2_c, n7_seg_driver_2_d, n7_seg_driver_2_e,
       n7_seg_driver_2_f, n7_seg_driver_2_g, xnor_1_out, xnor_2_out, xnor_3_out, xnor_4_out, xnor_5_out,
       xnor_6_out, xnor_7_out, xnor_8_out, xnor_9_out;

  J_K_Flip_Flop j_k_ff_1 (
    .J(and_5_out), .clk(and_5_out), .K(and_5_out), .Q(j_k_ff_1_q));  // open: Qn, preset, en, reset
  xnor xnor_1 (xnor_1_out, in_2, j_k_ff_1_q);
  Counter_driver counter_driver_1 (
    .\UP_DƠN (in_2), .SIGNAL(and_5_out), .Q1(counter_driver_1_q1), .Q2(counter_driver_1_q2),
    .Q7(counter_driver_1_q7), .Q8(counter_driver_1_q8), .Q4(counter_driver_1_q4), .Q5(counter_driver_1_q5),
    .Q3(counter_driver_1_q3), .Q6(counter_driver_1_q6));
  and and_1 (and_1_out, xnor_1_out, in_1);
  _7_seg_Driver u_7_seg_driver_1 (
    .a(n7_seg_driver_1_a), .b(n7_seg_driver_1_b), .c(n7_seg_driver_1_c), .d(n7_seg_driver_1_d),
    .e(n7_seg_driver_1_e), .f(n7_seg_driver_1_f), .g(n7_seg_driver_1_g), .B0(counter_driver_1_q1),
    .B1(counter_driver_1_q2), .B2(counter_driver_1_q3), .B3(counter_driver_1_q4));
  _7_seg_Driver u_7_seg_driver_2 (
    .a(n7_seg_driver_2_a), .b(n7_seg_driver_2_b), .c(n7_seg_driver_2_c), .d(n7_seg_driver_2_d),
    .e(n7_seg_driver_2_e), .f(n7_seg_driver_2_f), .g(n7_seg_driver_2_g), .B0(counter_driver_1_q5),
    .B1(counter_driver_1_q6), .B2(counter_driver_1_q7), .B3(counter_driver_1_q8));
  _7_Segment_Display u_7_segment_display_1 (
    .g(n7_seg_driver_2_g), .f(n7_seg_driver_2_f), .a(n7_seg_driver_2_a), .b(n7_seg_driver_2_b),
    .e(n7_seg_driver_2_e), .d(n7_seg_driver_2_d), .c(n7_seg_driver_2_c));  // open: dp
  b2d b2d_1 (
    .D(in_3), .C(in_4), .B(in_5), .A(in_6), .a_2(b2d_1_a_2), .b_2(b2d_1_b_2), .c_2(b2d_1_c_2),
    .d_2(b2d_1_d_2), .e(b2d_1_e), .f(b2d_1_f), .g(b2d_1_g));
  _7_Segment_Display u_7_segment_display_2 (
    .g(b2d_1_g), .f(b2d_1_f), .a(b2d_1_a_2), .b(b2d_1_b_2), .e(b2d_1_e), .d(b2d_1_d_2), .c(b2d_1_c_2));  // open: dp
  _7_Segment_Display u_7_segment_display_3 (
    .g(n7_seg_driver_1_g), .f(n7_seg_driver_1_f), .a(n7_seg_driver_1_a), .b(n7_seg_driver_1_b),
    .e(n7_seg_driver_1_e), .d(n7_seg_driver_1_d), .c(n7_seg_driver_1_c));  // open: dp
  b2d b2d_2 (
    .D(in_7), .C(in_8), .B(in_9), .A(in_10), .a_2(b2d_2_a_2), .b_2(b2d_2_b_2), .c_2(b2d_2_c_2),
    .d_2(b2d_2_d_2), .e(b2d_2_e), .f(b2d_2_f), .g(b2d_2_g));
  _7_Segment_Display u_7_segment_display_4 (
    .g(b2d_2_g), .f(b2d_2_f), .a(b2d_2_a_2), .b(b2d_2_b_2), .e(b2d_2_e), .d(b2d_2_d_2), .c(b2d_2_c_2));  // open: dp
  b2d b2d_3 (
    .D(in_11), .C(in_12), .B(in_13), .A(in_14), .a_2(b2d_3_a_2), .b_2(b2d_3_b_2), .c_2(b2d_3_c_2),
    .d_2(b2d_3_d_2), .e(b2d_3_e), .f(b2d_3_f), .g(b2d_3_g));
  _7_Segment_Display u_7_segment_display_5 (
    .g(b2d_3_g), .f(b2d_3_f), .a(b2d_3_a_2), .b(b2d_3_b_2), .e(b2d_3_e), .d(b2d_3_d_2), .c(b2d_3_c_2));  // open: dp
  xnor xnor_2 (xnor_2_out, in_7, in_15);
  xnor xnor_3 (xnor_3_out, in_8, in_16);
  xnor xnor_4 (xnor_4_out, in_9, in_17);
  xnor xnor_5 (xnor_5_out, in_10, 1'b1);
  xnor xnor_6 (xnor_6_out, in_3, in_11);
  xnor xnor_7 (xnor_7_out, in_4, in_12);
  xnor xnor_8 (xnor_8_out, in_5, in_13);
  xnor xnor_9 (xnor_9_out, in_6, in_14);
  and and_2 (and_2_out, xnor_2_out, xnor_3_out, xnor_4_out, xnor_5_out);
  _7_Segment_Display u_7_segment_display_6 (
    .g(b2d_4_g), .f(b2d_4_f), .a(b2d_4_a_2), .b(b2d_4_b_2), .e(b2d_4_e), .d(b2d_4_d_2), .c(b2d_4_c_2));  // open: dp
  b2d b2d_4 (
    .D(in_15), .C(in_16), .B(in_17), .A(1'b1), .a_2(b2d_4_a_2), .b_2(b2d_4_b_2), .c_2(b2d_4_c_2),
    .d_2(b2d_4_d_2), .e(b2d_4_e), .f(b2d_4_f), .g(b2d_4_g));
  and and_3 (and_3_out, xnor_6_out, xnor_7_out, xnor_8_out, xnor_9_out);
  and and_4 (and_4_out, and_2_out, and_3_out);
  // Clock_Control clock_control_1: pin names not known; wires that end beside it: clock_control_1_p1, clock_control_1_p2, clock_control_1_p3, clock_control_1_p4, clock_control_1_p5, clock_control_1_p6, clock_control_1_p7, clock_control_1_p8, clock_control_1_p9, clock_control_1_p10, clock_control_1_p11, clock_control_1_p12, clock_control_1_p13, clock_control_1_p14, clock_control_1_p15, clock_control_1_p16, clock_control_1_p17, clock_control_1_p18, clock_control_1_p19, clock_control_1_p20, clock_control_1_p21, clock_control_1_p22, clock_control_1_p23, clock_control_1_p24, clock_control_1_p25, clock_control_1_p26, clock_control_1_p27, clock_control_1_p28, clock_control_1_p29, clock_control_1_p30
  and and_5 (and_5_out, and_4_out, and_1_out);
  _7_Segment_Display u_7_segment_display_7 (
    .g(clock_control_1_p8), .f(clock_control_1_p10), .a(clock_control_1_p12), .b(clock_control_1_p15),
    .e(clock_control_1_p9), .d(clock_control_1_p11), .c(clock_control_1_p13), .dp(clock_control_1_p16));
  _7_Segment_Display u_7_segment_display_8 (
    .g(clock_control_1_p1), .f(clock_control_1_p3), .a(clock_control_1_p5), .b(clock_control_1_p7),
    .e(clock_control_1_p2), .d(clock_control_1_p4), .c(clock_control_1_p6));  // open: dp
  and and_6 (clock_control_1_p14, j_k_ff_1_q, clock_1_out);
  _7_Segment_Display u_7_segment_display_9 (
    .g(clock_control_1_p17), .f(clock_control_1_p19), .a(clock_control_1_p21), .b(clock_control_1_p23),
    .e(clock_control_1_p18), .d(clock_control_1_p20), .c(clock_control_1_p22));  // open: dp
  _7_Segment_Display u_7_segment_display_10 (
    .g(clock_control_1_p24), .f(clock_control_1_p26), .a(clock_control_1_p28), .b(clock_control_1_p30),
    .e(clock_control_1_p25), .d(clock_control_1_p27), .c(clock_control_1_p29));  // open: dp
  Clock clock_1 (.out(clock_1_out));
endmodule

module Counter_driver (
  input  \UP_DƠN ,
  input  SIGNAL,
  output Q1,
  output Q2,
  output Q7,
  output Q8,
  output Q4,
  output Q5,
  output Q3,
  output Q6
);

  wire and_1_out, and_2_out, and_3_out, and_4_out, and_5_out, and_6_out, and_7_out, and_8_out, and_9_out,
       and_10_out, and_11_out, and_12_out, and_13_out, and_14_out, and_15_out, and_16_out, and_17_out,
       j_k_ff_1_qn, j_k_ff_2_qn, j_k_ff_3_qn, j_k_ff_5_qn, j_k_ff_6_qn, j_k_ff_7_qn, nand_1_out, nand_2_out,
       not_1_out, not_2_out, or_1_out, or_2_out, or_3_out, or_4_out, or_5_out, or_6_out;

  and and_1 (and_1_out, and_2_out, and_9_out);
  not not_1 (not_1_out, \UP_DƠN );
  and and_2 (and_2_out, Q4, Q3, Q2, Q1);
  J_K_Flip_Flop j_k_ff_1 (
    .J(1'b1), .clk(SIGNAL), .K(1'b1), .Q(Q1), .Qn(j_k_ff_1_qn), .preset(and_1_out), .en(nand_2_out),
    .reset(and_9_out));
  and and_3 (and_3_out, not_1_out, Q1);
  and and_4 (and_4_out, j_k_ff_1_qn, \UP_DƠN );
  or or_1 (or_1_out, and_3_out, and_4_out);
  J_K_Flip_Flop j_k_ff_2 (
    .J(or_1_out), .clk(SIGNAL), .K(or_1_out), .Q(Q2), .Qn(j_k_ff_2_qn), .en(nand_2_out), .reset(and_9_out));  // open: preset
  and and_5 (and_5_out, and_3_out, Q2);
  and and_6 (and_6_out, j_k_ff_2_qn, and_4_out);
  or or_2 (or_2_out, and_5_out, and_6_out);
  J_K_Flip_Flop j_k_ff_3 (
    .J(or_2_out), .clk(SIGNAL), .K(or_2_out), .Q(Q3), .Qn(j_k_ff_3_qn), .en(nand_2_out), .reset(and_9_out));  // open: preset
  and and_7 (and_7_out, and_5_out, Q3);
  and and_8 (and_8_out, j_k_ff_3_qn, and_6_out);
  and and_9 (and_9_out, Q2, Q4);
  or or_3 (or_3_out, and_7_out, and_8_out);
  J_K_Flip_Flop j_k_ff_4 (
    .J(or_3_out), .clk(SIGNAL), .K(or_3_out), .Q(Q4), .preset(and_1_out), .en(nand_2_out), .reset(and_9_out));  // open: Qn
  and and_10 (and_10_out, Q4, Q2);
  nand nand_1 (nand_1_out, Q4, Q3, Q2, Q1);
  not not_2 (not_2_out, \UP_DƠN );
  J_K_Flip_Flop j_k_ff_5 (
    .J(1'b1), .clk(and_10_out), .K(1'b1), .Q(Q5), .Qn(j_k_ff_5_qn), .en(nand_2_out));  // open: preset, reset
  and and_11 (and_11_out, not_2_out, Q5);
  and and_12 (and_12_out, j_k_ff_5_qn, \UP_DƠN );
  nand nand_2 (nand_2_out, nand_1_out, not_1_out, and_13_out);
  or or_4 (or_4_out, and_11_out, and_12_out);
  and and_13 (and_13_out, Q5, Q7);
  J_K_Flip_Flop j_k_ff_6 (
    .J(or_4_out), .clk(and_10_out), .K(or_4_out), .Q(Q6), .Qn(j_k_ff_6_qn), .en(nand_2_out));  // open: preset, reset
  and and_14 (and_14_out, and_11_out, Q6);
  and and_15 (and_15_out, j_k_ff_6_qn, and_12_out);
  or or_5 (or_5_out, and_14_out, and_15_out);
  J_K_Flip_Flop j_k_ff_7 (
    .J(or_5_out), .clk(and_10_out), .K(or_5_out), .Q(Q7), .Qn(j_k_ff_7_qn), .en(nand_2_out));  // open: preset, reset
  and and_16 (and_16_out, j_k_ff_7_qn, and_15_out);
  and and_17 (and_17_out, and_14_out, Q7);
  or or_6 (or_6_out, and_17_out, and_16_out);
  J_K_Flip_Flop j_k_ff_8 (
    .J(or_6_out), .clk(and_10_out), .K(or_6_out), .Q(Q8), .en(nand_2_out));  // open: Qn, preset, reset
endmodule
