// Logisim project inputnumber.circ as structural Verilog: 2 circuits, main circuit main
module main (
  input  in_1,
  input  in_2,
  input  in_3,
  input  in_4,
  input  [3:0] in_5,
  input  [3:0] in_6
);

  wire b2d_1_a_2, b2d_1_b_2, b2d_1_c_2, b2d_1_d_2, b2d_1_e, b2d_1_f, b2d_1_g, b2d_2_a_2, b2d_2_b_2,
       b2d_2_c_2, b2d_2_d_2, b2d_2_e, b2d_2_f, b2d_2_g;

  b2d b2d_1 (
    .D(in_5[3]), .C(in_5[2]), .B(in_5[1]), .A(in_5[0]), .a_2(b2d_1_a_2), .b_2(b2d_1_b_2), .c_2(b2d_1_c_2),
    .d_2(b2d_1_d_2), .e(b2d_1_e), .f(b2d_1_f), .g(b2d_1_g));
  b2d b2d_2 (
    .D(in_1), .C(in_2), .B(in_3), .A(in_4), .a_2(b2d_2_a_2), .b_2(b2d_2_b_2), .c_2(b2d_2_c_2),
    .d_2(b2d_2_d_2), .e(b2d_2_e), .f(b2d_2_f), .g(b2d_2_g));
  _7_Segment_Display u_7_segment_display_1 (
    .g(b2d_1_g), .f(b2d_1_f), .a(b2d_1_a_2), .b(b2d_1_b_2), .e(b2d_1_e), .d(b2d_1_d_2), .c(b2d_1_c_2));  // open: dp
  Hex_Digit_Display hex_digit_display_1 (.value(in_6));  // open: dp
  _7_Segment_Display u_7_segment_display_2 (
    .g(b2d_2_g), .f(b2d_2_f), .a(b2d_2_a_2), .b(b2d_2_b_2), .e(b2d_2_e), .d(b2d_2_d_2), .c(b2d_2_c_2));  // open: dp
endmodule

module b2d (
  input  D,
  input  C,
  input  B,
  input  A,
  output a_2,
  output b_2,
  output c_2,
  output d_2,
  output e,
  output f,
  output g
);

  wire and_1_out, and_2_out, and_3_out, and_4_out, and_5_out, and_6_out, and_7_out, and_8_out, and_9_out,
       and_10_out, and_11_out, and_12_out, and_13_out, and_14_out, and_15_out, and_16_out, not_1_out,
       not_2_out, not_3_out, not_4_out, not_5_out, not_6_out, not_7_out, not_8_out, not_9_out, not_10_out,
       not_11_out, not_12_out, not_13_out, not_14_out, not_15_out, not_16_out, not_17_out, not_18_out,
       not_19_out, not_20_out, not_21_out;

  not not_1 (not_1_out, C);
  and and_1 (and_1_out, not_1_out, not_2_out);
  not not_2 (not_2_out, A);
  and and_2 (and_2_out, C, A);
  not not_3 (not_3_out, C);
  not not_4 (not_4_out, B);
  and and_3 (and_3_out, not_4_out, not_5_out);
  not not_5 (not_5_out, A);
  and and_4 (and_4_out, B, A);
  not not_6 (not_6_out, B);
  or or_1 (c_2, not_6_out, A, C);
  not not_7 (not_7_out, C);
  and and_5 (and_5_out, not_7_out, not_8_out);
  not not_8 (not_8_out, A);
  not not_9 (not_9_out, C);
  and and_6 (and_6_out, not_9_out, B);
  and and_7 (and_7_out, B, not_10_out);
  not not_10 (not_10_out, A);
  not not_11 (not_11_out, B);
  and and_8 (and_8_out, C, not_11_out, A);
  not not_12 (not_12_out, C);
  and and_9 (and_9_out, not_12_out, not_13_out);
  not not_13 (not_13_out, A);
  and and_10 (and_10_out, B, not_14_out);
  not not_14 (not_14_out, A);
  not not_15 (not_15_out, B);
  and and_11 (and_11_out, not_15_out, not_16_out);
  not not_16 (not_16_out, A);
  and and_12 (and_12_out, C, not_17_out);
  not not_17 (not_17_out, B);
  and and_13 (and_13_out, C, not_18_out);
  not not_18 (not_18_out, A);
  not not_19 (not_19_out, C);
  and and_14 (and_14_out, not_19_out, B);
  and and_15 (and_15_out, C, not_20_out);
  not not_20 (not_20_out, B);
  and and_16 (and_16_out, C, not_21_out);
  not not_21 (not_21_out, A);
  or or_2 (a_2, and_1_out, B, and_2_out, D);
  or or_3 (b_2, not_3_out, and_3_out, and_4_out);
  or or_4 (d_2, and_5_out, and_6_out, and_7_out, and_8_out, D);
  or or_5 (e, and_9_out, and_10_out);
  or or_6 (f, and_11_out, and_12_out, and_13_out, D);
  or or_7 (g, and_14_out, and_15_out, and_16_out, D);
endmodule
